// Logisim project logisim 入门.circ as structural Verilog: 25 circuits, main circuit 按钮
module \从零开始  (
  input  [3:0] y,
  input  [3:0] x,
  output [3:0] test,
  output [3:0] out_4
);

  wire [3:0] undriven, undriven_2, xor_1_out;

  // Probe on y
  // Probe on x
  // Probe on x
  assign xor_1_out = ~undriven ^ undriven_2;  // XOR_Gate xor_1, 4 bits wide
  // Probe on test
  assign test = y ^ x;  // XOR_Gate xor_2, 4 bits wide
  // Probe on y
  assign out_4 = test & y;  // AND_Gate and_1, 4 bits wide

  // Other names for the same wires on the sheet: TY[3:0] = y
endmodule

module \不同颜色线缆  (
  input  \引脚类型不对 ,
  input  [1:0] in_2,
  input  in_3
);

  wire undriven;
  wire [1:0] nand_2_out;
  wire [1:1] undriven_2;

  nand nand_1 (\引脚类型不对 , 1'b1, 1'b0, undriven, 1'b0);
  assign nand_2_out = ~(in_2 & in_2 & {undriven_2[1], in_3});  // NAND_Gate nand_2, 2 bits wide
  // Pins of 1 and 2 bits meet at {undriven_2[1], in_3}

  // Notes on the sheet:
  //   深绿色表示低电平
  //   蓝色表示未知状态
  //   灰色表示飞线
  //   亮绿色表示高电平
  //   红色表示信号冲突
  //   黑色表示多位总线
  //   橙色表示位宽不匹配
  //   华中科技大学计算机学院 计算机组成原理
  //   红色表示输入有悬空或错误
endmodule

module \分线器使用  (
  input  [7:0] in_1
);

  \不同颜色线缆  \u_不同颜色线缆_1  ();  // open: in_2, in_3, 引脚类型不对

  // Notes on the sheet:
  //   分线器使用方法
  //   8分3，两个3位，一个2位
  //   分线器不分输入输出，可反向使用进行线缆汇总
  //   华中科技大学计算机学院 计算机组成原理
  //   8分二，高位在下
  //   8分二，高位在上
  //   只分部分位，位宽不对称
  //   只分1位，如取符号位
  //   8分8
endmodule

module \按钮  (
);

  wire button_1_out;

  Button button_1 (.out(button_1_out));
  LED #(.active("true")) led_1 (.in(button_1_out));
endmodule

module \摇杆  (
  output [3:0] out_1,
  output [3:0] out_2
);

  Joystick #(.bits(4)) joystick_1 (.x(out_1), .y(out_2));
endmodule

module \键盘  (
  output [6:0] out_1
);

  wire clock_1_out;

  Keyboard #(.Char_bit_width(7), .buflen(32), .trigger("rising")) keyboard_1 (
    .clk(clock_1_out), .re(1'b1), .data(out_1));  // open: clr, avail
  Clock #(.highDuration(1), .lowDuration(1)) clock_1 (.out(clock_1_out));
  TTY #(.Char_bit_width(7), .rows(8), .cols(32), .trigger("rising")) tty_1 (
    .data(out_1), .clk(clock_1_out));  // open: we, clr
endmodule

module \LED点阵  (
  input  [6:0] x,
  input  [6:0] x_2,
  input  [6:0] x_3,
  input  [6:0] x_4,
  input  [6:0] x_5
);

  DotMatrix #(.inputtype("column"), .matrixcols(5), .matrixrows(7), .persist(0), .dotshape("square")) dotmatrix_1 (
    .col0(x), .col1(x_5), .col2(x_2), .col3(x_3), .col4(x_4));
endmodule

module \数码管  (
  input  [3:0] in_1,
  input  [3:0] in_2,
  input  in_3,
  input  [3:0] in_4
);

  _7_Segment_Display #(.active("true")) u_7_segment_display_1 (
    .g(in_1[3]), .f(in_1[2]), .a(in_1[1]), .b(in_1[0]), .e(in_2[3]), .d(in_2[2]), .c(in_2[1]), .dp(in_2[0]));
  Hex_Digit_Display hex_digit_display_1 (.value(in_4), .dp(in_3));
endmodule

module \奇偶校验  (
  input  [4:0] x,
  output out_2
);

  buf odd_parity_1 (out_2, ~x[1]);  // Odd_Parity Odd_Parity
endmodule

module \三态门  (
  input  in_1,
  input  in_2,
  output out_3
);

  assign out_3 = in_2 ? ~in_1 : 1'bz;  // Controlled_Inverter controlled_inverter_1
  LED #(.active("true")) led_1 (.in(out_3));
endmodule

module \复用器  (
  input  [3:0] in_1,
  input  [3:0] in_2,
  input  [3:0] in_3,
  input  [3:0] in_4,
  input  [1:0] in_5,
  output [3:0] out_6
);

  Multiplexer #(.select(2), .width(4), .disabled("Z"), .enable("true")) multiplexer_1 (
    .in0(in_1), .in1(in_2), .in2(in_3), .in3(in_4), .out(out_6), .sel(in_5));  // open: en
endmodule

module \解复用器  (
  input  [3:0] in_1,
  input  [1:0] in_2,
  output [3:0] out_3,
  output [3:0] out_4,
  output [3:0] out_5,
  output [3:0] out_6
);

  Demultiplexer #(.select(2), .width(4), .tristate("false"), .disabled("Z"), .enable("true")) demultiplexer_1 (
    .out0(out_3), .out1(out_4), .out2(out_5), .out3(out_6), .in(in_1), .sel(in_2));  // open: en
endmodule

module \解码器  (
  input  [1:0] in_1
);

  wire decoder_1_out0, decoder_1_out1, decoder_1_out2, decoder_1_out3;

  Decoder #(.select(2), .tristate("false"), .disabled("Z"), .enable("true")) decoder_1 (
    .out0(decoder_1_out0), .out1(decoder_1_out1), .out2(decoder_1_out2), .out3(decoder_1_out3), .sel(in_1));  // open: en
endmodule

module \优先编码器  (
  input  in_1,
  input  in_2,
  input  in_3,
  input  in_4,
  input  in_5,
  input  in_6,
  input  in_7,
  input  in_8,
  output [2:0] out_9,
  output out_10
);

  Priority_Encoder #(.select(3), .disabled("Z")) priority_encoder_1 (
    .in0(in_1), .in1(in_2), .in2(in_3), .in3(in_4), .in4(in_5), .in5(in_6), .in6(in_7), .in7(in_8),
    .out(out_9), .gs(out_10));  // open: en_out, en_in
endmodule

module \位选择器  (
  input  [7:0] in_1,
  input  [2:0] in_2,
  output out_3
);

  BitSelector #(.width(8), .group(1)) bitselector_1 (.in(in_1), .out(out_3), .sel(in_2));
  Register #(.width(8), .trigger("rising"), .Select("low")) register_1 ();  // open: D, en, Q, clk, clr
endmodule

module \D触发器  (
  input  in_1,
  output out_2
);

  wire clock_1_out;

  Clock #(.highDuration(1), .lowDuration(1)) clock_1 (.out(clock_1_out));
  D_Flip_Flop #(.trigger("rising"), .Pre_Clr_Positions("LEGACY"), .NegatePresetClear("false"), .enable("true"), .NewFFLayout("false")) d_ff_1 (
    .clk(clock_1_out), .D(in_1), .Q(out_2));  // open: Qn, preset, en, reset
endmodule

module \寄存器  (
  input  [15:0] in_1,
  input  in_2,
  output [15:0] out_3
);

  wire clock_1_out;

  // Probe on in_1
  Register #(.width(16), .trigger("rising"), .Select("low")) register_1 (
    .D(in_1), .Q(out_3), .clk(clock_1_out), .clr(in_2));  // open: en
  Clock #(.highDuration(1), .lowDuration(1)) clock_1 (.out(clock_1_out));
endmodule

module \计数器  (
  input  in_1,
  input  [7:0] in_2,
  input  in_3,
  input  in_4,
  output [7:0] out_5
);

  wire clock_1_out, counter_1_carry;

  // Probe on in_2
  Clock #(.highDuration(1), .lowDuration(1)) clock_1 (.out(clock_1_out));
  // Probe on out_5
  Counter #(.width(8), .max('hff), .ongoal("wrap"), .trigger("rising"), .behavior("old")) counter_1 (
    .load(in_1), .D(in_2), .count(in_3), .Q(out_5), .carry(counter_1_carry), .clk(clock_1_out), .clr(in_4));  // open: preset
endmodule

module \移位寄存器  (
  input  [7:0] in_1,
  input  in_2,
  input  in_3,
  output out_4,
  output [7:0] out_5
);

  wire clock_1_out;

  Clock #(.highDuration(1), .lowDuration(1)) clock_1 (.out(clock_1_out));
  Shift_Register #(.width(1), .length(8), .parallel("true"), .trigger("rising")) shift_register_1 (
    .in(in_3), .clk(clock_1_out), .out(out_4), .load(in_2), .d0(in_1[7]), .q0(out_5[7]), .d1(in_1[6]),
    .q1(out_5[6]), .d2(in_1[5]), .q2(out_5[5]), .d3(in_1[4]), .q3(out_5[4]), .d4(in_1[3]), .q4(out_5[3]),
    .d5(in_1[2]), .q5(out_5[2]), .d6(in_1[1]), .q6(out_5[1]), .d7(in_1[0]), .q7(out_5[0]));  // open: shift, clr
endmodule

module \随机数产生器  (
  input  in_1,
  output [7:0] out_2
);

  wire clock_1_out;

  Clock #(.highDuration(1), .lowDuration(1)) clock_1 (.out(clock_1_out));
  // Probe on out_2
  Random #(.width(8), .seed(0), .trigger("rising")) random_1 (
    .clk(clock_1_out), .out(out_2), .clr(in_1));  // open: next
endmodule

module \毛刺现象  (
);

  wire and_1_out, and_2_out, buffer_1_out, clock_1_out, not_1_out, not_2_out;

  Clock #(.highDuration(1), .lowDuration(1)) clock_1 (.out(clock_1_out));
  Counter #(.width(8), .max('hff), .ongoal("wrap"), .trigger("rising"), .behavior("old")) counter_1 (.clk(clock_1_out));  // open: load, D, count, Q, carry, clr, preset
  Counter #(.width(8), .max('hff), .ongoal("wrap"), .trigger("rising"), .behavior("old")) counter_2 (.clk(clock_1_out));  // open: load, D, count, Q, carry, clr, preset
  buf buffer_1 (buffer_1_out, clock_1_out);
  not not_1 (not_1_out, clock_1_out);
  not not_2 (not_2_out, clock_1_out);
  and and_1 (and_1_out, not_1_out, clock_1_out);
  and and_2 (and_2_out, not_2_out, buffer_1_out);
  Counter #(.width(8), .max('hff), .ongoal("wrap"), .trigger("rising"), .behavior("old")) counter_3 (.clk(and_1_out));  // open: load, D, count, Q, carry, clr, preset
  Counter #(.width(8), .max('hff), .ongoal("wrap"), .trigger("rising"), .behavior("old")) counter_4 (.clk(and_2_out));  // open: load, D, count, Q, carry, clr, preset

  // Notes on the sheet:
  //   增加缓冲器，使得延迟一样，避免毛刺
  //   此计数器不可能计数，但试试看？为什么？
  //   修改后正常
  //   用计数器观察调试毛刺
endmodule

module \存储器  (
  input  [7:0] in_1,
  input  [7:0] in_2,
  output [7:0] out_3,
  output [7:0] out_4
);

  RAM #(.addrWidth(8), .dataWidth(8), .bus("combined"), .Select("high")) ram_1 (
    .addr(in_1), .data(out_3));  // open: sel, clk, ld, clr
  ROM #(.addrWidth(8), .dataWidth(8), .Select("high")) rom_1 (.addr(in_2), .data(out_4));
endmodule

module \震荡电路  (
  input  in_1,
  output out_2
);

  nand nand_1 (out_2, in_1, out_2);

  // Notes on the sheet:
  //   尝试修改输入引脚的电平,输入输出存在反馈，导致电路状态不稳定
  //   如出现类似情况，尝试去掉部分回路连接直至故障消除
  //   华中科技大学计算机学院 计算机组成原理
endmodule

module \信号冲突  (
  input  in_1,
  input  in_2,
  output out_3
);


  assign in_2 = in_1;
  assign out_3 = in_1;

  // Notes on the sheet:
  //   输入相同时无问题，不同时出错，红色显示
  //   华中科技大学计算机学院 计算机组成原理
endmodule

module \异常反馈  (
  input  in_1,
  input  in_2,
  output out_3
);

  wire not_1_out;

  Multiplexer #(.select(1), .width(1), .disabled("Z"), .enable("false")) multiplexer_1 (
    .in0(in_1), .in1(in_2), .out(out_3), .sel(not_1_out));
  not not_1 (not_1_out, out_3);

  // Notes on the sheet:
  //   类似震荡
endmodule
